// Logisim project choon_circuit.circ as structural Verilog: 8 circuits, main circuit main
module main (
);

  wire and_1_out, and_2_out, and_3_out, and_4_out, and_5_out, and_6_out, and_7_out, and_8_out, and_9_out,
       and_10_out, and_11_out, and_12_out, and_13_out, and_14_out, and_15_out, and_16_out, and_25_out,
       and_26_out, and_27_out, and_28_out, button_3_out, disappear_1_out_3, disappear_2_out_3,
       disappear_3_out_3, disappear_4_out_3, disappear_5_out_3, disappear_6_out_3, disappear_7_out_3,
       disappear_8_out_3, disappear_9_out_3, disappear_10_out_3, disappear_11_out_3, disappear_12_out_3,
       disappear_13_out_3, disappear_14_out_3, disappear_15_out_3, disappear_16_out_3, l1, l2, l3, l4, l5,
       l6, l7, l8, l9, level1L, level1R, level2L, level2R, level3L, level3R, level4L, level4R, level5L,
       level5R, level6L, level6R, level7L, level7R, level8L, level8R, light1, light2, light3, light4, light5,
       light6, light7, light8, not_9_out, not_10_out, not_11_out, not_12_out, not_13_out, not_14_out,
       not_15_out, not_16_out, offE, or_1_out, or_2_out, or_3_out, or_4_out, or_5_out, or_6_out, or_7_out,
       or_8_out, or_9_out, or_10_out, or_11_out, or_12_out, or_13_out, or_14_out, or_15_out, or_16_out,
       or_17_out, or_18_out, or_19_out, or_20_out, or_21_out, or_22_out, or_23_out, or_24_out, r1, r2, r3,
       r4, r5, r6, r7, r8, re1L, re1R, re2L, re2R, re3L, re3R, re4L, re4R, re5L, re5R, re6L, re6R, re7L,
       re7R, re8L, re8R, reset, result1L, result1R, result2L, result2R, result3L, result3R, result4L,
       result4R, result5L, result5R, result6L, result6R, result7L, result7R, result8L, result8R, start,
       theEnd, w1, w2, w3, w4, w5, w6, w7, w8;
  wire [7:0] A, A1, A2, A3, A4, A5, A6, A7, A8, B, B1, B2, B3, B4, B5, B6, B7, B8, C, C1, C2, C3, C4, C5, C6,
       C7, C8, Ca, Cb, Cc, Cd, Ce, Cf, Cg, Ch, D, D1, d1L, d1R, D2, d2L, d2R, D3, d3L, d3R, D4, d4L, d4R, D5,
       d5L, d5R, D6, d6L, d6R, D7, d7L, d7R, D8, d8L, d8R, E, E1, E2, E3, E4, E5, E6, E7, E8, Ea, Eb, Ec, Ed,
       Ee, Ef, Eg, Eh, F, F1, F2, F3, F4, F5, F6, F7, F8, G, G1, G2, G3, G4, G5, G6, G7, G8, H, H1, H2, H3,
       H4, H5, H6, H7, H8, or_25_out, random_1_out, Sa, Sb, Sc, Sd, Se, Sf, Sg, Sh, Ua, Ub, Uc, Ud, Ue, Uf,
       Ug, Uh;

  Button button_1 (.out(reset));
  Button button_2 (.out(start));
  Button button_3 (.out(button_3_out));
  Random random_1 (.clr(reset), .next(reset), .clk(reset), .out(random_1_out));
  DotMatrix #(.matrixcols(8), .matrixrows(8)) dotmatrix_1 (
    .col0(A), .col1(B), .col2(C), .col3(D), .col4(E), .col5(F), .col6(G), .col7(H));
  assign {light1, light2, light3, light4, light5, light6, light7, light8} = {{7{button_3_out}}, button_3_out};  // Bit_Extender bit_extender_1
  not not_1 (w1, random_1_out[0]);
  not not_2 (w2, random_1_out[1]);
  not not_3 (w3, random_1_out[2]);
  not not_4 (w4, random_1_out[3]);
  not not_5 (w5, random_1_out[4]);
  not not_6 (w6, random_1_out[5]);
  not not_7 (w7, random_1_out[6]);
  not not_8 (w8, random_1_out[7]);
  DotMatrix #(.matrixcols(8), .matrixrows(8)) dotmatrix_2 (
    .col0(A1), .col1(B1), .col2(C1), .col3(D1), .col4(E1), .col5(F1), .col6(G1), .col7(H1));
  Button button_4 (.out(level1L));
  Button button_5 (.out(level1R));
  LED led_1 (.in(result1L));
  LED led_2 (.in(result1R));
  stone stone_1 (.whichone(random_1_out[0]), .choose(level1L), .out_3(re1L));
  stone stone_2 (.whichone(random_1_out[1]), .choose(level2L), .out_3(re2L));
  stone stone_3 (.whichone(random_1_out[2]), .choose(level3L), .out_3(re3L));
  stone stone_4 (.whichone(random_1_out[3]), .choose(level4L), .out_3(re4L));
  stone stone_5 (.whichone(random_1_out[4]), .choose(level5L), .out_3(re5L));
  stone stone_6 (.whichone(random_1_out[5]), .choose(level6L), .out_3(re6L));
  stone stone_7 (.whichone(random_1_out[6]), .choose(level7L), .out_3(re7L));
  stone stone_8 (.whichone(random_1_out[7]), .choose(level8L), .out_3(re8L));
  Button button_6 (.out(level2L));
  Button button_7 (.out(level2R));
  DotMatrix #(.matrixcols(8), .matrixrows(8)) dotmatrix_3 (
    .col0(A2), .col1(B2), .col2(C2), .col3(D2), .col4(E2), .col5(F2), .col6(G2), .col7(H2));
  and and_1 (and_1_out, re1L, l1);
  and and_2 (and_2_out, re2L, l2);
  and and_3 (and_3_out, re3L, l3);
  and and_4 (and_4_out, re4L, l4);
  and and_5 (and_5_out, re5L, l5);
  and and_6 (and_6_out, re6L, l6);
  and and_7 (and_7_out, re7L, l7);
  and and_8 (and_8_out, re8L, l8);
  LED led_3 (.in(result2L));
  LED led_4 (.in(result2R));
  DotMatrix #(.matrixcols(8), .matrixrows(8)) dotmatrix_4 (
    .col0(A3), .col1(B3), .col2(C3), .col3(D3), .col4(E3), .col5(F3), .col6(G3), .col7(H3));
  Button button_8 (.out(level3L));
  Button button_9 (.out(level3R));
  T_Flip_Flop t_ff_1 (.Q(result1L), .reset(light1), .preset(and_1_out));  // open: T, clk, Qn
  T_Flip_Flop t_ff_2 (.Q(result2L), .reset(light2), .preset(and_2_out));  // open: T, clk, Qn
  T_Flip_Flop t_ff_3 (.Q(result3L), .reset(light3), .preset(and_3_out));  // open: T, clk, Qn
  T_Flip_Flop t_ff_4 (.Q(result4L), .reset(light4), .preset(and_4_out));  // open: T, clk, Qn
  T_Flip_Flop t_ff_5 (.Q(result5L), .reset(light5), .preset(and_5_out));  // open: T, clk, Qn
  T_Flip_Flop t_ff_6 (.Q(result6L), .reset(light6), .preset(and_6_out));  // open: T, clk, Qn
  T_Flip_Flop t_ff_7 (.Q(result7L), .reset(light7), .preset(and_7_out));  // open: T, clk, Qn
  T_Flip_Flop t_ff_8 (.Q(result8L), .reset(light8), .preset(and_8_out));  // open: T, clk, Qn
  LED led_5 (.in(result3L));
  LED led_6 (.in(result3R));
  Button button_10 (.out(level4L));
  Button button_11 (.out(level4R));
  DotMatrix #(.matrixcols(8), .matrixrows(8)) dotmatrix_5 (
    .col0(A4), .col1(B4), .col2(C4), .col3(D4), .col4(E4), .col5(F4), .col6(G4), .col7(H4));
  LED led_7 (.in(result4L));
  LED led_8 (.in(result4R));
  DotMatrix #(.matrixcols(8), .matrixrows(8)) dotmatrix_6 (
    .col0(A5), .col1(B5), .col2(C5), .col3(D5), .col4(E5), .col5(F5), .col6(G5), .col7(H5));
  Button button_12 (.out(level5L));
  Button button_13 (.out(level5R));
  LED led_9 (.in(result5L));
  LED led_10 (.in(result5R));
  Button button_14 (.out(level6L));
  Button button_15 (.out(level6R));
  stone stone_9 (.whichone(w1), .choose(level1R), .out_3(re1R));
  stone stone_10 (.whichone(w2), .choose(level2R), .out_3(re2R));
  stone stone_11 (.whichone(w3), .choose(level3R), .out_3(re3R));
  stone stone_12 (.whichone(w4), .choose(level4R), .out_3(re4R));
  stone stone_13 (.whichone(w5), .choose(level5R), .out_3(re5R));
  stone stone_14 (.whichone(w6), .choose(level6R), .out_3(re6R));
  stone stone_15 (.whichone(w7), .choose(level7R), .out_3(re7R));
  stone stone_16 (.whichone(w8), .choose(level8R), .out_3(re8R));
  DotMatrix #(.matrixcols(8), .matrixrows(8)) dotmatrix_7 (
    .col0(A6), .col1(B6), .col2(C6), .col3(D6), .col4(E6), .col5(F6), .col6(G6), .col7(H6));
  LED led_11 (.in(result6L));
  LED led_12 (.in(result6R));
  and and_9 (and_9_out, re1R, l1);
  and and_10 (and_10_out, re2R, l2);
  and and_11 (and_11_out, re3R, l3);
  and and_12 (and_12_out, re4R, l4);
  and and_13 (and_13_out, re5R, l5);
  and and_14 (and_14_out, re6R, l6);
  and and_15 (and_15_out, re7R, l7);
  and and_16 (and_16_out, re8R, l8);
  DotMatrix #(.matrixcols(8), .matrixrows(8)) dotmatrix_8 (
    .col0(A7), .col1(B7), .col2(C7), .col3(D7), .col4(E7), .col5(F7), .col6(G7), .col7(H7));
  Button button_16 (.out(level7L));
  Button button_17 (.out(level7R));
  T_Flip_Flop t_ff_9 (.Q(result1R), .reset(light1), .preset(and_9_out));  // open: T, clk, Qn
  T_Flip_Flop t_ff_10 (.Q(result2R), .reset(light2), .preset(and_10_out));  // open: T, clk, Qn
  T_Flip_Flop t_ff_11 (.Q(result3R), .reset(light3), .preset(and_11_out));  // open: T, clk, Qn
  T_Flip_Flop t_ff_12 (.Q(result4R), .reset(light4), .preset(and_12_out));  // open: T, clk, Qn
  T_Flip_Flop t_ff_13 (.Q(result5R), .reset(light5), .preset(and_13_out));  // open: T, clk, Qn
  T_Flip_Flop t_ff_14 (.Q(result6R), .reset(light6), .preset(and_14_out));  // open: T, clk, Qn
  T_Flip_Flop t_ff_15 (.Q(result7R), .reset(light7), .preset(and_15_out));  // open: T, clk, Qn
  T_Flip_Flop t_ff_16 (.Q(result8R), .reset(light8), .preset(and_16_out));  // open: T, clk, Qn
  LED led_13 (.in(result7L));
  LED led_14 (.in(result7R));
  Button button_18 (.out(level8L));
  Button button_19 (.out(level8R));
  DotMatrix #(.matrixcols(8), .matrixrows(8)) dotmatrix_9 (
    .col0(A8), .col1(B8), .col2(C8), .col3(D8), .col4(E8), .col5(F8), .col6(G8), .col7(H8));
  DotMatrix #(.matrixcols(8), .matrixrows(8)) dotmatrix_10 (
    .col0(Sa), .col1(Sb), .col2(Sc), .col3(Sd), .col4(Se), .col5(Sf), .col6(Sg), .col7(Sh));
  LED led_15 (.in(result8L));
  LED led_16 (.in(result8R));
  or or_1 (or_1_out, level1L, level1R);
  and and_17 (r1, l1, or_2_out);
  or or_2 (or_2_out, re1L, re1R);
  or or_3 (or_3_out, level2L, level2R);
  and and_18 (r8, l8, or_4_out);
  or or_4 (or_4_out, re8L, re8R);
  Button button_20 (.out(offE));
  Button button_21 (.out(theEnd));
  or or_5 (or_5_out, light1, or_1_out);
  or or_6 (or_6_out, light2, or_3_out);
  DotMatrix #(.matrixcols(8), .matrixrows(8)) dotmatrix_11 (
    .col0(Ua), .col1(Ub), .col2(Uc), .col3(Ud), .col4(Ue), .col5(Uf), .col6(Ug), .col7(Uh));
  DotMatrix #(.matrixcols(8), .matrixrows(8)) dotmatrix_12 (
    .col0(Ca), .col1(Cb), .col2(Cc), .col3(Cd), .col4(Ce), .col5(Cf), .col6(Cg), .col7(Ch));
  people people_1 (
    .S(start), .R(or_5_out), .A(A), .out_6(B), .out_7(C), .out_8(D), .out_9(E), .out_10(F), .out_12(G),
    .out_13(H));  // open: T, CLK, o
  people people_2 (
    .S(r1), .R(or_6_out), .A(A1), .out_6(B1), .out_7(C1), .out_8(D1), .out_9(E1), .out_10(F1), .out_12(G1),
    .out_13(H1));  // open: T, CLK, o
  people people_3 (
    .S(r8), .R(theEnd), .A(A8), .out_6(B8), .out_7(C8), .out_8(D8), .out_9(E8), .out_10(F8), .out_12(G8),
    .out_13(H8));  // open: T, CLK, o
  DotMatrix #(.matrixcols(8), .matrixrows(8)) dotmatrix_13 (
    .col0(Ca), .col1(Cb), .col2(Cc), .col3(Cd), .col4(Ce), .col5(Cf), .col6(Cg), .col7(Ch));
  DotMatrix #(.matrixcols(8), .matrixrows(8)) dotmatrix_14 (
    .col0(Ea), .col1(Eb), .col2(Ec), .col3(Ed), .col4(Ee), .col5(Ef), .col6(Eg), .col7(Eh));
  or or_7 (or_7_out, re2L, re2R);
  or or_8 (or_8_out, re3L, re3R);
  DotMatrix #(.matrixcols(8), .matrixrows(8)) dotmatrix_15 (
    .col0(Sa), .col1(Sb), .col2(Sc), .col3(Sd), .col4(Se), .col5(Sf), .col6(Sg), .col7(Sh));
  and and_19 (r2, l2, or_7_out);
  or or_9 (or_9_out, level3L, level3R);
  and and_20 (r3, l3, or_8_out);
  or or_10 (or_10_out, level4L, level4R);
  or or_11 (or_11_out, light3, or_9_out);
  or or_12 (or_12_out, light4, or_10_out);
  DotMatrix #(.matrixcols(8), .matrixrows(8)) dotmatrix_16 (
    .col0(Sa), .col1(Sb), .col2(Sc), .col3(Sd), .col4(Se), .col5(Sf), .col6(Sg), .col7(Sh));
  people people_4 (
    .S(r2), .R(or_11_out), .A(A2), .out_6(B2), .out_7(C2), .out_8(D2), .out_9(E2), .out_10(F2), .out_12(G2),
    .out_13(H2));  // open: T, CLK, o
  people people_5 (
    .S(r3), .R(or_12_out), .A(A3), .out_6(B3), .out_7(C3), .out_8(D3), .out_9(E3), .out_10(F3), .out_12(G3),
    .out_13(H3));  // open: T, CLK, o
  or or_13 (or_13_out, re4L, re4R);
  or or_14 (or_14_out, re5L, re5R);
  and and_21 (r4, l4, or_13_out);
  or or_15 (or_15_out, light5, or_16_out);
  or or_16 (or_16_out, level5L, level5R);
  and and_22 (r5, l5, or_14_out);
  or or_17 (or_17_out, light6, or_18_out);
  or or_18 (or_18_out, level6L, level6R);
  people people_6 (
    .S(r4), .R(or_15_out), .A(A4), .out_6(B4), .out_7(C4), .out_8(D4), .out_9(E4), .out_10(F4), .out_12(G4),
    .out_13(H4));  // open: T, CLK, o
  people people_7 (
    .S(r5), .R(or_17_out), .A(A5), .out_6(B5), .out_7(C5), .out_8(D5), .out_9(E5), .out_10(F5), .out_12(G5),
    .out_13(H5));  // open: T, CLK, o
  T_Flip_Flop t_ff_17 (.Q(l1), .reset(or_25_out[7]), .preset(start));  // open: T, clk, Qn
  or or_19 (or_19_out, re6L, re6R);
  or or_20 (or_20_out, re7L, re7R);
  T_Flip_Flop t_ff_18 (.Q(l2), .reset(or_25_out[6]), .preset(r1));  // open: T, clk, Qn
  and and_23 (r6, l6, or_19_out);
  or or_21 (or_21_out, level7L, level7R);
  and and_24 (r7, l7, or_20_out);
  or or_22 (or_22_out, level8L, level8R);
  or or_23 (or_23_out, light7, or_21_out);
  or or_24 (or_24_out, light8, or_22_out);
  T_Flip_Flop t_ff_19 (.Q(l3), .reset(or_25_out[5]), .preset(r2));  // open: T, clk, Qn
  T_Flip_Flop t_ff_20 (.Q(l4), .reset(or_25_out[4]), .preset(r3));  // open: T, clk, Qn
  T_Flip_Flop t_ff_21 (.Q(l5), .reset(or_25_out[3]), .preset(r4));  // open: T, clk, Qn
  assign or_25_out = {light1, light2, light3, light4, light5, light6, light7, light8} | d1L | d1R | d2L | d2R | d3L | d3R | d4L | d4R | d5L | d6L | d6R | d7L | d7R | d8L | d8R;  // OR_Gate or_25, 8 bits wide
  people people_8 (
    .S(r6), .R(or_23_out), .A(A6), .out_6(B6), .out_7(C6), .out_8(D6), .out_9(E6), .out_10(F6), .out_12(G6),
    .out_13(H6));  // open: T, CLK, o
  people people_9 (
    .S(r7), .R(or_24_out), .A(A7), .out_6(B7), .out_7(C7), .out_8(D7), .out_9(E7), .out_10(F7), .out_12(G7),
    .out_13(H7));  // open: T, CLK, o
  T_Flip_Flop t_ff_22 (.Q(l6), .reset(or_25_out[2]), .preset(r5));  // open: T, clk, Qn
  T_Flip_Flop t_ff_23 (.Q(l9), .reset(offE), .preset(r8));  // open: T, clk, Qn
  T_Flip_Flop t_ff_24 (.Q(l7), .reset(or_25_out[1]), .preset(r6));  // open: T, clk, Qn
  T_Flip_Flop t_ff_25 (.Q(l8), .reset(or_25_out[0]), .preset(r7));  // open: T, clk, Qn
  not not_9 (not_9_out, w5);
  not not_10 (not_10_out, w7);
  not not_11 (not_11_out, w1);
  not not_12 (not_12_out, w3);
  disappear disappear_1 (.in_1(level1L), .in_2(not_11_out), .out_3(disappear_1_out_3));
  disappear disappear_2 (.in_1(level3L), .in_2(not_12_out), .out_3(disappear_2_out_3));
  disappear disappear_3 (.in_1(level5L), .in_2(not_9_out), .out_3(disappear_3_out_3));
  disappear disappear_4 (.in_1(level7L), .in_2(not_10_out), .out_3(disappear_4_out_3));
  disappear disappear_5 (.in_1(level1R), .in_2(w1), .out_3(disappear_5_out_3));
  disappear disappear_6 (.in_1(level3R), .in_2(w3), .out_3(disappear_6_out_3));
  disappear disappear_7 (.in_1(level5R), .in_2(w5), .out_3(disappear_7_out_3));
  disappear disappear_8 (.in_1(level7R), .in_2(w7), .out_3(disappear_8_out_3));
  assign d1L = {{7{disappear_1_out_3}}, disappear_1_out_3};  // Bit_Extender bit_extender_2
  assign d3L = {{7{disappear_2_out_3}}, disappear_2_out_3};  // Bit_Extender bit_extender_3
  assign d5L = {{7{disappear_3_out_3}}, disappear_3_out_3};  // Bit_Extender bit_extender_4
  assign d7L = {{7{disappear_4_out_3}}, disappear_4_out_3};  // Bit_Extender bit_extender_5
  assign d1R = {{7{disappear_5_out_3}}, disappear_5_out_3};  // Bit_Extender bit_extender_6
  assign d3R = {{7{disappear_6_out_3}}, disappear_6_out_3};  // Bit_Extender bit_extender_7
  assign d5R = {{7{disappear_7_out_3}}, disappear_7_out_3};  // Bit_Extender bit_extender_8
  assign d7R = {{7{disappear_8_out_3}}, disappear_8_out_3};  // Bit_Extender bit_extender_9
  not not_13 (not_13_out, w2);
  not not_14 (not_14_out, w4);
  not not_15 (not_15_out, w6);
  not not_16 (not_16_out, w8);
  disappear disappear_9 (.in_1(level2L), .in_2(not_13_out), .out_3(disappear_9_out_3));
  disappear disappear_10 (.in_1(level4L), .in_2(not_14_out), .out_3(disappear_10_out_3));
  disappear disappear_11 (.in_1(level6L), .in_2(not_15_out), .out_3(disappear_11_out_3));
  disappear disappear_12 (.in_1(level8L), .in_2(not_16_out), .out_3(disappear_12_out_3));
  disappear disappear_13 (.in_1(level2R), .in_2(w2), .out_3(disappear_13_out_3));
  disappear disappear_14 (.in_1(level4R), .in_2(w4), .out_3(disappear_14_out_3));
  disappear disappear_15 (.in_1(level6R), .in_2(w6), .out_3(disappear_15_out_3));
  disappear disappear_16 (.in_1(level8R), .in_2(w8), .out_3(disappear_16_out_3));
  assign d2L = {{7{disappear_9_out_3}}, disappear_9_out_3};  // Bit_Extender bit_extender_10
  assign d4L = {{7{disappear_10_out_3}}, disappear_10_out_3};  // Bit_Extender bit_extender_11
  assign d6L = {{7{disappear_11_out_3}}, disappear_11_out_3};  // Bit_Extender bit_extender_12
  assign d8L = {{7{disappear_12_out_3}}, disappear_12_out_3};  // Bit_Extender bit_extender_13
  assign d2R = {{7{disappear_13_out_3}}, disappear_13_out_3};  // Bit_Extender bit_extender_14
  assign d4R = {{7{disappear_14_out_3}}, disappear_14_out_3};  // Bit_Extender bit_extender_15
  assign d6R = {{7{disappear_15_out_3}}, disappear_15_out_3};  // Bit_Extender bit_extender_16
  assign d8R = {{7{disappear_16_out_3}}, disappear_16_out_3};  // Bit_Extender bit_extender_17
  and and_25 (and_25_out, l9, theEnd);
  and and_26 (and_26_out, l9, theEnd);
  and and_27 (and_27_out, l9, theEnd);
  and and_28 (and_28_out, l9, theEnd);
  Ett ett_1 (
    .S(and_25_out), .R(offE), .A(Ea), .out_6(Eb), .out_7(Ec), .out_8(Ed), .out_9(Ee), .out_10(Ef),
    .out_12(Eg), .out_13(Eh));  // open: T, CLK, o
  Ctt ctt_1 (
    .S(and_26_out), .R(offE), .A(Ca), .out_6(Cb), .out_7(Cc), .out_8(Cd), .out_9(Ce), .out_10(Cf),
    .out_12(Cg), .out_13(Ch));  // open: T, CLK, o
  S s_1 (
    .in_1(and_27_out), .R(offE), .A(Sa), .out_6(Sb), .out_7(Sc), .out_8(Sd), .out_9(Se), .out_10(Sf),
    .out_12(Sg), .out_13(Sh));  // open: T, CLK, o
  U u_1 (
    .S(and_28_out), .R(offE), .A(Ua), .out_6(Ub), .out_7(Uc), .out_8(Ud), .out_9(Ue), .out_10(Uf),
    .out_12(Ug), .out_13(Uh));  // open: T, CLK, o

  // Other names for the same wires on the sheet: off[7:0] = {light1, light2, light3, light4, light5, light6, light7, light8};
  //   off8 = light8; off7 = light7; off6 = light6; off5 = light5; off4 = light4; off3 = light3; off2 = light2;
  //   off1 = light1

  // Notes on the sheet:
  //   랜덤으로 2진수 8개 받기 
  //   stone = and gate 이용해 한쪽은 누르면 1 한쪽은 눌러도 0
  //   다음 단계 건너뛰면 작동 안하도록 and gate 사용
  //   LED가 off 버튼 누르지 않는 이상 계속 켜져있도록 
  //   toggle flip flop 사용 S와 R부분에 연결해줌
  //   랜덤 stone의 결과를 받기위해 or gate 사용 
  //   다음 단계 건너뛰면 작동 안하도록 and gate 사용
  //   다음 단계 누르면 사라지도록 or gate에 연결 
  //   off 버튼 누르면 사람 사라지도록 or gate에 연결
  //   사람 시작 누르면 나타나도록 T flip flop의 S부분에 연결 
  //   off 누르면 사람 사라지도록 설정
  //   start을  누르면 l1 0->1 정답을 누르면 r1 0->1
  //   l2 0->1 순차적으로 단계가  진행됨
  //   off 누르면 모든 LED 꺼지도록 연결
  //   off 버튼과 오답 누르면 초기화
  //    0 0 -> 0
  //    0 1 -> 0
  //    1 0 -> 1
  //    1 1 -> 0
  //   xor와 and gate 연결하여 1 0만 1
  //   오답일 때 w가 0이 되어 회로가 초기화됨 
  //   순차적으로 진행되게 하기 위해 l9와 the End를 
  //   and gate로 연결 offE 누르면 모두 꺼짐
endmodule

module stone (
  input  whichone,
  input  choose,
  output out_3
);

  wire buffer_1_out;

  buf buffer_1 (buffer_1_out, choose);
  and and_1 (out_3, whichone, buffer_1_out);
endmodule

module people (
  input  S,
  input  T,
  input  CLK,
  input  R,
  output [7:0] A,
  output [7:0] out_6,
  output [7:0] out_7,
  output [7:0] out_8,
  output [7:0] out_9,
  output [7:0] out_10,
  output o,
  output [7:0] out_12,
  output [7:0] out_13
);

  wire A0, A1, A2, A3, A4, A5, A6, A7, B0, B1, B2, B3, B4, B5, B6, B7, C0, C1, C2, C3, C4, C5, C6, C7, D0,
       D1, D2, D3, D4, D5, D6, D7, E0, E1, E2, E3, E4, E5, E6, E7, F0, F1, F2, F3, F4, F5, F6, F7, G0, G1,
       G2, G3, G4, G5, G6, G7, H0, H1, H2, H3, H4, H5, H6, H7, t_ff_1_q;
  wire [7:0] bit_extender_1_out;

  T_Flip_Flop t_ff_1 (.T(T), .clk(CLK), .Q(t_ff_1_q), .Qn(o), .reset(R), .preset(S));
  assign bit_extender_1_out = {{7{t_ff_1_q}}, t_ff_1_q};  // Bit_Extender bit_extender_1
  assign {A7, A6, A5, A4, A3, A2, A1, A0} = {{7{bit_extender_1_out[0]}}, bit_extender_1_out[0]};  // Bit_Extender bit_extender_2
  assign {B7, B6, B5, B4, B3, B2, B1, B0} = {{7{bit_extender_1_out[1]}}, bit_extender_1_out[1]};  // Bit_Extender bit_extender_3
  assign {C7, C6, C5, C4, C3, C2, C1, C0} = {{7{bit_extender_1_out[2]}}, bit_extender_1_out[2]};  // Bit_Extender bit_extender_4
  assign {D7, D6, D5, D4, D3, D2, D1, D0} = {{7{bit_extender_1_out[3]}}, bit_extender_1_out[3]};  // Bit_Extender bit_extender_5
  assign {E7, E6, E5, E4, E3, E2, E1, E0} = {{7{bit_extender_1_out[4]}}, bit_extender_1_out[4]};  // Bit_Extender bit_extender_6
  assign {F7, F6, F5, F4, F3, F2, F1, F0} = {{7{bit_extender_1_out[5]}}, bit_extender_1_out[5]};  // Bit_Extender bit_extender_7
  assign {G7, G6, G5, G4, G3, G2, G1, G0} = {{7{bit_extender_1_out[6]}}, bit_extender_1_out[6]};  // Bit_Extender bit_extender_8
  assign {H7, H6, H5, H4, H3, H2, H1, H0} = {{7{bit_extender_1_out[7]}}, bit_extender_1_out[7]};  // Bit_Extender bit_extender_9
  stone stone_1 (.whichone(A0), .choose(1'b0), .out_3(A[0]));
  stone stone_2 (.whichone(A1), .choose(1'b0), .out_3(A[1]));
  stone stone_3 (.whichone(A2), .choose(1'b0), .out_3(A[2]));
  stone stone_4 (.whichone(A3), .choose(1'b0), .out_3(A[3]));
  stone stone_5 (.whichone(A4), .choose(1'b0), .out_3(A[4]));
  stone stone_6 (.whichone(A5), .choose(1'b0), .out_3(A[5]));
  stone stone_7 (.whichone(A6), .choose(1'b0), .out_3(A[6]));
  stone stone_8 (.whichone(A7), .choose(1'b0), .out_3(A[7]));
  stone stone_9 (.whichone(G0), .choose(1'b1), .out_3(out_12[0]));
  stone stone_10 (.whichone(G1), .choose(1'b0), .out_3(out_12[1]));
  stone stone_11 (.whichone(G2), .choose(1'b0), .out_3(out_12[2]));
  stone stone_12 (.whichone(G3), .choose(1'b1), .out_3(out_12[3]));
  stone stone_13 (.whichone(G4), .choose(1'b0), .out_3(out_12[4]));
  stone stone_14 (.whichone(G5), .choose(1'b0), .out_3(out_12[5]));
  stone stone_15 (.whichone(G6), .choose(1'b0), .out_3(out_12[6]));
  stone stone_16 (.whichone(G7), .choose(1'b0), .out_3(out_12[7]));
  stone stone_17 (.whichone(B0), .choose(1'b0), .out_3(out_6[0]));
  stone stone_18 (.whichone(B1), .choose(1'b0), .out_3(out_6[1]));
  stone stone_19 (.whichone(B2), .choose(1'b0), .out_3(out_6[2]));
  stone stone_20 (.whichone(B3), .choose(1'b0), .out_3(out_6[3]));
  stone stone_21 (.whichone(B4), .choose(1'b0), .out_3(out_6[4]));
  stone stone_22 (.whichone(B5), .choose(1'b0), .out_3(out_6[5]));
  stone stone_23 (.whichone(B6), .choose(1'b0), .out_3(out_6[6]));
  stone stone_24 (.whichone(B7), .choose(1'b0), .out_3(out_6[7]));
  stone stone_25 (.whichone(H0), .choose(1'b0), .out_3(out_13[0]));
  stone stone_26 (.whichone(H1), .choose(1'b0), .out_3(out_13[1]));
  stone stone_27 (.whichone(H2), .choose(1'b0), .out_3(out_13[2]));
  stone stone_28 (.whichone(H3), .choose(1'b0), .out_3(out_13[3]));
  stone stone_29 (.whichone(H4), .choose(1'b0), .out_3(out_13[4]));
  stone stone_30 (.whichone(H5), .choose(1'b0), .out_3(out_13[5]));
  stone stone_31 (.whichone(H6), .choose(1'b0), .out_3(out_13[6]));
  stone stone_32 (.whichone(H7), .choose(1'b0), .out_3(out_13[7]));
  stone stone_33 (.whichone(C0), .choose(1'b1), .out_3(out_7[0]));
  stone stone_34 (.whichone(C1), .choose(1'b0), .out_3(out_7[1]));
  stone stone_35 (.whichone(C2), .choose(1'b0), .out_3(out_7[2]));
  stone stone_36 (.whichone(C3), .choose(1'b1), .out_3(out_7[3]));
  stone stone_37 (.whichone(C4), .choose(1'b0), .out_3(out_7[4]));
  stone stone_38 (.whichone(C5), .choose(1'b0), .out_3(out_7[5]));
  stone stone_39 (.whichone(C6), .choose(1'b0), .out_3(out_7[6]));
  stone stone_40 (.whichone(C7), .choose(1'b0), .out_3(out_7[7]));
  stone stone_41 (.whichone(D0), .choose(1'b0), .out_3(out_8[0]));
  stone stone_42 (.whichone(D1), .choose(1'b1), .out_3(out_8[1]));
  stone stone_43 (.whichone(D2), .choose(1'b0), .out_3(out_8[2]));
  stone stone_44 (.whichone(D3), .choose(1'b1), .out_3(out_8[3]));
  stone stone_45 (.whichone(D4), .choose(1'b0), .out_3(out_8[4]));
  stone stone_46 (.whichone(D5), .choose(1'b0), .out_3(out_8[5]));
  stone stone_47 (.whichone(D6), .choose(1'b1), .out_3(out_8[6]));
  stone stone_48 (.whichone(D7), .choose(1'b1), .out_3(out_8[7]));
  stone stone_49 (.whichone(E0), .choose(1'b0), .out_3(out_9[0]));
  stone stone_50 (.whichone(E1), .choose(1'b0), .out_3(out_9[1]));
  stone stone_51 (.whichone(E2), .choose(1'b1), .out_3(out_9[2]));
  stone stone_52 (.whichone(E3), .choose(1'b1), .out_3(out_9[3]));
  stone stone_53 (.whichone(E4), .choose(1'b1), .out_3(out_9[4]));
  stone stone_54 (.whichone(E5), .choose(1'b1), .out_3(out_9[5]));
  stone stone_55 (.whichone(E6), .choose(1'b1), .out_3(out_9[6]));
  stone stone_56 (.whichone(E7), .choose(1'b1), .out_3(out_9[7]));
  stone stone_57 (.whichone(F0), .choose(1'b0), .out_3(out_10[0]));
  stone stone_58 (.whichone(F1), .choose(1'b1), .out_3(out_10[1]));
  stone stone_59 (.whichone(F2), .choose(1'b0), .out_3(out_10[2]));
  stone stone_60 (.whichone(F3), .choose(1'b1), .out_3(out_10[3]));
  stone stone_61 (.whichone(F4), .choose(1'b0), .out_3(out_10[4]));
  stone stone_62 (.whichone(F5), .choose(1'b0), .out_3(out_10[5]));
  stone stone_63 (.whichone(F6), .choose(1'b1), .out_3(out_10[6]));
  stone stone_64 (.whichone(F7), .choose(1'b1), .out_3(out_10[7]));

  // Notes on the sheet:
  //   choose가 0이면 버튼 눌렀을 때 0
  //   choose가 1이면 버튼 눌렀을 때 1
endmodule

module disappear (
  input  in_1,
  input  in_2,
  output out_3
);

  wire xor_1_out;

  xor xor_1 (xor_1_out, in_1, in_2);
  and and_1 (out_3, in_1, xor_1_out);
endmodule

module Ett (
  input  S,
  input  T,
  input  CLK,
  input  R,
  output [7:0] A,
  output [7:0] out_6,
  output [7:0] out_7,
  output [7:0] out_8,
  output [7:0] out_9,
  output [7:0] out_10,
  output o,
  output [7:0] out_12,
  output [7:0] out_13
);

  wire A0, A1, A2, A3, A4, A5, A6, A7, B0, B1, B2, B3, B4, B5, B6, B7, C0, C1, C2, C3, C4, C5, C6, C7, D0,
       D1, D2, D3, D4, D5, D6, D7, E0, E1, E2, E3, E4, E5, E6, E7, F0, F1, F2, F3, F4, F5, F6, F7, G0, G1,
       G2, G3, G4, G5, G6, G7, H0, H1, H2, H3, H4, H5, H6, H7, t_ff_1_q;
  wire [7:0] bit_extender_1_out;

  T_Flip_Flop t_ff_1 (.T(T), .clk(CLK), .Q(t_ff_1_q), .Qn(o), .reset(R), .preset(S));
  assign bit_extender_1_out = {{7{t_ff_1_q}}, t_ff_1_q};  // Bit_Extender bit_extender_1
  assign {A7, A6, A5, A4, A3, A2, A1, A0} = {{7{bit_extender_1_out[0]}}, bit_extender_1_out[0]};  // Bit_Extender bit_extender_2
  assign {B7, B6, B5, B4, B3, B2, B1, B0} = {{7{bit_extender_1_out[1]}}, bit_extender_1_out[1]};  // Bit_Extender bit_extender_3
  assign {C7, C6, C5, C4, C3, C2, C1, C0} = {{7{bit_extender_1_out[2]}}, bit_extender_1_out[2]};  // Bit_Extender bit_extender_4
  assign {D7, D6, D5, D4, D3, D2, D1, D0} = {{7{bit_extender_1_out[3]}}, bit_extender_1_out[3]};  // Bit_Extender bit_extender_5
  assign {E7, E6, E5, E4, E3, E2, E1, E0} = {{7{bit_extender_1_out[4]}}, bit_extender_1_out[4]};  // Bit_Extender bit_extender_6
  assign {F7, F6, F5, F4, F3, F2, F1, F0} = {{7{bit_extender_1_out[5]}}, bit_extender_1_out[5]};  // Bit_Extender bit_extender_7
  assign {G7, G6, G5, G4, G3, G2, G1, G0} = {{7{bit_extender_1_out[6]}}, bit_extender_1_out[6]};  // Bit_Extender bit_extender_8
  assign {H7, H6, H5, H4, H3, H2, H1, H0} = {{7{bit_extender_1_out[7]}}, bit_extender_1_out[7]};  // Bit_Extender bit_extender_9
  stone stone_1 (.whichone(A0), .choose(1'b1), .out_3(A[0]));
  stone stone_2 (.whichone(A1), .choose(1'b1), .out_3(A[1]));
  stone stone_3 (.whichone(A2), .choose(1'b1), .out_3(A[2]));
  stone stone_4 (.whichone(A3), .choose(1'b1), .out_3(A[3]));
  stone stone_5 (.whichone(A4), .choose(1'b1), .out_3(A[4]));
  stone stone_6 (.whichone(A5), .choose(1'b1), .out_3(A[5]));
  stone stone_7 (.whichone(A6), .choose(1'b1), .out_3(A[6]));
  stone stone_8 (.whichone(A7), .choose(1'b1), .out_3(A[7]));
  stone stone_9 (.whichone(G0), .choose(1'b1), .out_3(out_12[0]));
  stone stone_10 (.whichone(G1), .choose(1'b0), .out_3(out_12[1]));
  stone stone_11 (.whichone(G2), .choose(1'b0), .out_3(out_12[2]));
  stone stone_12 (.whichone(G3), .choose(1'b0), .out_3(out_12[3]));
  stone stone_13 (.whichone(G4), .choose(1'b1), .out_3(out_12[4]));
  stone stone_14 (.whichone(G5), .choose(1'b0), .out_3(out_12[5]));
  stone stone_15 (.whichone(G6), .choose(1'b0), .out_3(out_12[6]));
  stone stone_16 (.whichone(G7), .choose(1'b1), .out_3(out_12[7]));
  stone stone_17 (.whichone(B0), .choose(1'b1), .out_3(out_6[0]));
  stone stone_18 (.whichone(B1), .choose(1'b0), .out_3(out_6[1]));
  stone stone_19 (.whichone(B2), .choose(1'b0), .out_3(out_6[2]));
  stone stone_20 (.whichone(B3), .choose(1'b0), .out_3(out_6[3]));
  stone stone_21 (.whichone(B4), .choose(1'b1), .out_3(out_6[4]));
  stone stone_22 (.whichone(B5), .choose(1'b0), .out_3(out_6[5]));
  stone stone_23 (.whichone(B6), .choose(1'b0), .out_3(out_6[6]));
  stone stone_24 (.whichone(B7), .choose(1'b1), .out_3(out_6[7]));
  stone stone_25 (.whichone(H0), .choose(1'b1), .out_3(out_13[0]));
  stone stone_26 (.whichone(H1), .choose(1'b0), .out_3(out_13[1]));
  stone stone_27 (.whichone(H2), .choose(1'b0), .out_3(out_13[2]));
  stone stone_28 (.whichone(H3), .choose(1'b0), .out_3(out_13[3]));
  stone stone_29 (.whichone(H4), .choose(1'b1), .out_3(out_13[4]));
  stone stone_30 (.whichone(H5), .choose(1'b0), .out_3(out_13[5]));
  stone stone_31 (.whichone(H6), .choose(1'b0), .out_3(out_13[6]));
  stone stone_32 (.whichone(H7), .choose(1'b1), .out_3(out_13[7]));
  stone stone_33 (.whichone(C0), .choose(1'b1), .out_3(out_7[0]));
  stone stone_34 (.whichone(C1), .choose(1'b0), .out_3(out_7[1]));
  stone stone_35 (.whichone(C2), .choose(1'b0), .out_3(out_7[2]));
  stone stone_36 (.whichone(C3), .choose(1'b0), .out_3(out_7[3]));
  stone stone_37 (.whichone(C4), .choose(1'b1), .out_3(out_7[4]));
  stone stone_38 (.whichone(C5), .choose(1'b0), .out_3(out_7[5]));
  stone stone_39 (.whichone(C6), .choose(1'b0), .out_3(out_7[6]));
  stone stone_40 (.whichone(C7), .choose(1'b1), .out_3(out_7[7]));
  stone stone_41 (.whichone(D0), .choose(1'b1), .out_3(out_8[0]));
  stone stone_42 (.whichone(D1), .choose(1'b0), .out_3(out_8[1]));
  stone stone_43 (.whichone(D2), .choose(1'b0), .out_3(out_8[2]));
  stone stone_44 (.whichone(D3), .choose(1'b0), .out_3(out_8[3]));
  stone stone_45 (.whichone(D4), .choose(1'b1), .out_3(out_8[4]));
  stone stone_46 (.whichone(D5), .choose(1'b0), .out_3(out_8[5]));
  stone stone_47 (.whichone(D6), .choose(1'b0), .out_3(out_8[6]));
  stone stone_48 (.whichone(D7), .choose(1'b1), .out_3(out_8[7]));
  stone stone_49 (.whichone(E0), .choose(1'b1), .out_3(out_9[0]));
  stone stone_50 (.whichone(E1), .choose(1'b0), .out_3(out_9[1]));
  stone stone_51 (.whichone(E2), .choose(1'b0), .out_3(out_9[2]));
  stone stone_52 (.whichone(E3), .choose(1'b0), .out_3(out_9[3]));
  stone stone_53 (.whichone(E4), .choose(1'b1), .out_3(out_9[4]));
  stone stone_54 (.whichone(E5), .choose(1'b0), .out_3(out_9[5]));
  stone stone_55 (.whichone(E6), .choose(1'b0), .out_3(out_9[6]));
  stone stone_56 (.whichone(E7), .choose(1'b1), .out_3(out_9[7]));
  stone stone_57 (.whichone(F0), .choose(1'b1), .out_3(out_10[0]));
  stone stone_58 (.whichone(F1), .choose(1'b0), .out_3(out_10[1]));
  stone stone_59 (.whichone(F2), .choose(1'b0), .out_3(out_10[2]));
  stone stone_60 (.whichone(F3), .choose(1'b0), .out_3(out_10[3]));
  stone stone_61 (.whichone(F4), .choose(1'b1), .out_3(out_10[4]));
  stone stone_62 (.whichone(F5), .choose(1'b0), .out_3(out_10[5]));
  stone stone_63 (.whichone(F6), .choose(1'b0), .out_3(out_10[6]));
  stone stone_64 (.whichone(F7), .choose(1'b1), .out_3(out_10[7]));
endmodule

module Ctt (
  input  S,
  input  T,
  input  CLK,
  input  R,
  output [7:0] A,
  output [7:0] out_6,
  output [7:0] out_7,
  output [7:0] out_8,
  output [7:0] out_9,
  output [7:0] out_10,
  output o,
  output [7:0] out_12,
  output [7:0] out_13
);

  wire A0, A1, A2, A3, A4, A5, A6, A7, B0, B1, B2, B3, B4, B5, B6, B7, C0, C1, C2, C3, C4, C5, C6, C7, D0,
       D1, D2, D3, D4, D5, D6, D7, E0, E1, E2, E3, E4, E5, E6, E7, F0, F1, F2, F3, F4, F5, F6, F7, G0, G1,
       G2, G3, G4, G5, G6, G7, H0, H1, H2, H3, H4, H5, H6, H7, t_ff_1_q;
  wire [7:0] bit_extender_1_out;

  T_Flip_Flop t_ff_1 (.T(T), .clk(CLK), .Q(t_ff_1_q), .Qn(o), .reset(R), .preset(S));
  assign bit_extender_1_out = {{7{t_ff_1_q}}, t_ff_1_q};  // Bit_Extender bit_extender_1
  assign {A7, A6, A5, A4, A3, A2, A1, A0} = {{7{bit_extender_1_out[0]}}, bit_extender_1_out[0]};  // Bit_Extender bit_extender_2
  assign {B7, B6, B5, B4, B3, B2, B1, B0} = {{7{bit_extender_1_out[1]}}, bit_extender_1_out[1]};  // Bit_Extender bit_extender_3
  assign {C7, C6, C5, C4, C3, C2, C1, C0} = {{7{bit_extender_1_out[2]}}, bit_extender_1_out[2]};  // Bit_Extender bit_extender_4
  assign {D7, D6, D5, D4, D3, D2, D1, D0} = {{7{bit_extender_1_out[3]}}, bit_extender_1_out[3]};  // Bit_Extender bit_extender_5
  assign {E7, E6, E5, E4, E3, E2, E1, E0} = {{7{bit_extender_1_out[4]}}, bit_extender_1_out[4]};  // Bit_Extender bit_extender_6
  assign {F7, F6, F5, F4, F3, F2, F1, F0} = {{7{bit_extender_1_out[5]}}, bit_extender_1_out[5]};  // Bit_Extender bit_extender_7
  assign {G7, G6, G5, G4, G3, G2, G1, G0} = {{7{bit_extender_1_out[6]}}, bit_extender_1_out[6]};  // Bit_Extender bit_extender_8
  assign {H7, H6, H5, H4, H3, H2, H1, H0} = {{7{bit_extender_1_out[7]}}, bit_extender_1_out[7]};  // Bit_Extender bit_extender_9
  stone stone_1 (.whichone(A0), .choose(1'b1), .out_3(A[0]));
  stone stone_2 (.whichone(A1), .choose(1'b1), .out_3(A[1]));
  stone stone_3 (.whichone(A2), .choose(1'b1), .out_3(A[2]));
  stone stone_4 (.whichone(A3), .choose(1'b1), .out_3(A[3]));
  stone stone_5 (.whichone(A4), .choose(1'b1), .out_3(A[4]));
  stone stone_6 (.whichone(A5), .choose(1'b1), .out_3(A[5]));
  stone stone_7 (.whichone(A6), .choose(1'b1), .out_3(A[6]));
  stone stone_8 (.whichone(A7), .choose(1'b1), .out_3(A[7]));
  stone stone_9 (.whichone(G0), .choose(1'b1), .out_3(out_12[0]));
  stone stone_10 (.whichone(G1), .choose(1'b0), .out_3(out_12[1]));
  stone stone_11 (.whichone(G2), .choose(1'b0), .out_3(out_12[2]));
  stone stone_12 (.whichone(G3), .choose(1'b0), .out_3(out_12[3]));
  stone stone_13 (.whichone(G4), .choose(1'b0), .out_3(out_12[4]));
  stone stone_14 (.whichone(G5), .choose(1'b0), .out_3(out_12[5]));
  stone stone_15 (.whichone(G6), .choose(1'b0), .out_3(out_12[6]));
  stone stone_16 (.whichone(G7), .choose(1'b1), .out_3(out_12[7]));
  stone stone_17 (.whichone(B0), .choose(1'b1), .out_3(out_6[0]));
  stone stone_18 (.whichone(B1), .choose(1'b0), .out_3(out_6[1]));
  stone stone_19 (.whichone(B2), .choose(1'b0), .out_3(out_6[2]));
  stone stone_20 (.whichone(B3), .choose(1'b0), .out_3(out_6[3]));
  stone stone_21 (.whichone(B4), .choose(1'b0), .out_3(out_6[4]));
  stone stone_22 (.whichone(B5), .choose(1'b0), .out_3(out_6[5]));
  stone stone_23 (.whichone(B6), .choose(1'b0), .out_3(out_6[6]));
  stone stone_24 (.whichone(B7), .choose(1'b1), .out_3(out_6[7]));
  stone stone_25 (.whichone(H0), .choose(1'b1), .out_3(out_13[0]));
  stone stone_26 (.whichone(H1), .choose(1'b0), .out_3(out_13[1]));
  stone stone_27 (.whichone(H2), .choose(1'b0), .out_3(out_13[2]));
  stone stone_28 (.whichone(H3), .choose(1'b0), .out_3(out_13[3]));
  stone stone_29 (.whichone(H4), .choose(1'b0), .out_3(out_13[4]));
  stone stone_30 (.whichone(H5), .choose(1'b0), .out_3(out_13[5]));
  stone stone_31 (.whichone(H6), .choose(1'b0), .out_3(out_13[6]));
  stone stone_32 (.whichone(H7), .choose(1'b1), .out_3(out_13[7]));
  stone stone_33 (.whichone(C0), .choose(1'b1), .out_3(out_7[0]));
  stone stone_34 (.whichone(C1), .choose(1'b0), .out_3(out_7[1]));
  stone stone_35 (.whichone(C2), .choose(1'b0), .out_3(out_7[2]));
  stone stone_36 (.whichone(C3), .choose(1'b0), .out_3(out_7[3]));
  stone stone_37 (.whichone(C4), .choose(1'b0), .out_3(out_7[4]));
  stone stone_38 (.whichone(C5), .choose(1'b0), .out_3(out_7[5]));
  stone stone_39 (.whichone(C6), .choose(1'b0), .out_3(out_7[6]));
  stone stone_40 (.whichone(C7), .choose(1'b1), .out_3(out_7[7]));
  stone stone_41 (.whichone(D0), .choose(1'b1), .out_3(out_8[0]));
  stone stone_42 (.whichone(D1), .choose(1'b0), .out_3(out_8[1]));
  stone stone_43 (.whichone(D2), .choose(1'b0), .out_3(out_8[2]));
  stone stone_44 (.whichone(D3), .choose(1'b0), .out_3(out_8[3]));
  stone stone_45 (.whichone(D4), .choose(1'b0), .out_3(out_8[4]));
  stone stone_46 (.whichone(D5), .choose(1'b0), .out_3(out_8[5]));
  stone stone_47 (.whichone(D6), .choose(1'b0), .out_3(out_8[6]));
  stone stone_48 (.whichone(D7), .choose(1'b1), .out_3(out_8[7]));
  stone stone_49 (.whichone(E0), .choose(1'b1), .out_3(out_9[0]));
  stone stone_50 (.whichone(E1), .choose(1'b0), .out_3(out_9[1]));
  stone stone_51 (.whichone(E2), .choose(1'b0), .out_3(out_9[2]));
  stone stone_52 (.whichone(E3), .choose(1'b0), .out_3(out_9[3]));
  stone stone_53 (.whichone(E4), .choose(1'b0), .out_3(out_9[4]));
  stone stone_54 (.whichone(E5), .choose(1'b0), .out_3(out_9[5]));
  stone stone_55 (.whichone(E6), .choose(1'b0), .out_3(out_9[6]));
  stone stone_56 (.whichone(E7), .choose(1'b1), .out_3(out_9[7]));
  stone stone_57 (.whichone(F0), .choose(1'b1), .out_3(out_10[0]));
  stone stone_58 (.whichone(F1), .choose(1'b0), .out_3(out_10[1]));
  stone stone_59 (.whichone(F2), .choose(1'b0), .out_3(out_10[2]));
  stone stone_60 (.whichone(F3), .choose(1'b0), .out_3(out_10[3]));
  stone stone_61 (.whichone(F4), .choose(1'b0), .out_3(out_10[4]));
  stone stone_62 (.whichone(F5), .choose(1'b0), .out_3(out_10[5]));
  stone stone_63 (.whichone(F6), .choose(1'b0), .out_3(out_10[6]));
  stone stone_64 (.whichone(F7), .choose(1'b1), .out_3(out_10[7]));
endmodule

module S (
  input  in_1,
  input  T,
  input  CLK,
  input  R,
  output [7:0] A,
  output [7:0] out_6,
  output [7:0] out_7,
  output [7:0] out_8,
  output [7:0] out_9,
  output [7:0] out_10,
  output o,
  output [7:0] out_12,
  output [7:0] out_13
);

  wire A0, A1, A2, A3, A4, A5, A6, A7, B0, B1, B2, B3, B4, B5, B6, B7, C0, C1, C2, C3, C4, C5, C6, C7, D0,
       D1, D2, D3, D4, D5, D6, D7, E0, E1, E2, E3, E4, E5, E6, E7, F0, F1, F2, F3, F4, F5, F6, F7, G0, G1,
       G2, G3, G4, G5, G6, G7, H0, H1, H2, H3, H4, H5, H6, H7, t_ff_1_q;
  wire [7:0] bit_extender_1_out;

  T_Flip_Flop t_ff_1 (.T(T), .clk(CLK), .Q(t_ff_1_q), .Qn(o), .reset(R), .preset(in_1));
  assign bit_extender_1_out = {{7{t_ff_1_q}}, t_ff_1_q};  // Bit_Extender bit_extender_1
  assign {A7, A6, A5, A4, A3, A2, A1, A0} = {{7{bit_extender_1_out[0]}}, bit_extender_1_out[0]};  // Bit_Extender bit_extender_2
  assign {B7, B6, B5, B4, B3, B2, B1, B0} = {{7{bit_extender_1_out[1]}}, bit_extender_1_out[1]};  // Bit_Extender bit_extender_3
  assign {C7, C6, C5, C4, C3, C2, C1, C0} = {{7{bit_extender_1_out[2]}}, bit_extender_1_out[2]};  // Bit_Extender bit_extender_4
  assign {D7, D6, D5, D4, D3, D2, D1, D0} = {{7{bit_extender_1_out[3]}}, bit_extender_1_out[3]};  // Bit_Extender bit_extender_5
  assign {E7, E6, E5, E4, E3, E2, E1, E0} = {{7{bit_extender_1_out[4]}}, bit_extender_1_out[4]};  // Bit_Extender bit_extender_6
  assign {F7, F6, F5, F4, F3, F2, F1, F0} = {{7{bit_extender_1_out[5]}}, bit_extender_1_out[5]};  // Bit_Extender bit_extender_7
  assign {G7, G6, G5, G4, G3, G2, G1, G0} = {{7{bit_extender_1_out[6]}}, bit_extender_1_out[6]};  // Bit_Extender bit_extender_8
  assign {H7, H6, H5, H4, H3, H2, H1, H0} = {{7{bit_extender_1_out[7]}}, bit_extender_1_out[7]};  // Bit_Extender bit_extender_9
  stone stone_1 (.whichone(A0), .choose(1'b1), .out_3(A[0]));
  stone stone_2 (.whichone(A1), .choose(1'b0), .out_3(A[1]));
  stone stone_3 (.whichone(A2), .choose(1'b0), .out_3(A[2]));
  stone stone_4 (.whichone(A3), .choose(1'b1), .out_3(A[3]));
  stone stone_5 (.whichone(A4), .choose(1'b1), .out_3(A[4]));
  stone stone_6 (.whichone(A5), .choose(1'b1), .out_3(A[5]));
  stone stone_7 (.whichone(A6), .choose(1'b1), .out_3(A[6]));
  stone stone_8 (.whichone(A7), .choose(1'b1), .out_3(A[7]));
  stone stone_9 (.whichone(G0), .choose(1'b1), .out_3(out_12[0]));
  stone stone_10 (.whichone(G1), .choose(1'b0), .out_3(out_12[1]));
  stone stone_11 (.whichone(G2), .choose(1'b0), .out_3(out_12[2]));
  stone stone_12 (.whichone(G3), .choose(1'b1), .out_3(out_12[3]));
  stone stone_13 (.whichone(G4), .choose(1'b0), .out_3(out_12[4]));
  stone stone_14 (.whichone(G5), .choose(1'b0), .out_3(out_12[5]));
  stone stone_15 (.whichone(G6), .choose(1'b0), .out_3(out_12[6]));
  stone stone_16 (.whichone(G7), .choose(1'b1), .out_3(out_12[7]));
  stone stone_17 (.whichone(B0), .choose(1'b1), .out_3(out_6[0]));
  stone stone_18 (.whichone(B1), .choose(1'b0), .out_3(out_6[1]));
  stone stone_19 (.whichone(B2), .choose(1'b0), .out_3(out_6[2]));
  stone stone_20 (.whichone(B3), .choose(1'b1), .out_3(out_6[3]));
  stone stone_21 (.whichone(B4), .choose(1'b0), .out_3(out_6[4]));
  stone stone_22 (.whichone(B5), .choose(1'b0), .out_3(out_6[5]));
  stone stone_23 (.whichone(B6), .choose(1'b0), .out_3(out_6[6]));
  stone stone_24 (.whichone(B7), .choose(1'b1), .out_3(out_6[7]));
  stone stone_25 (.whichone(H0), .choose(1'b1), .out_3(out_13[0]));
  stone stone_26 (.whichone(H1), .choose(1'b1), .out_3(out_13[1]));
  stone stone_27 (.whichone(H2), .choose(1'b1), .out_3(out_13[2]));
  stone stone_28 (.whichone(H3), .choose(1'b1), .out_3(out_13[3]));
  stone stone_29 (.whichone(H4), .choose(1'b0), .out_3(out_13[4]));
  stone stone_30 (.whichone(H5), .choose(1'b0), .out_3(out_13[5]));
  stone stone_31 (.whichone(H6), .choose(1'b0), .out_3(out_13[6]));
  stone stone_32 (.whichone(H7), .choose(1'b1), .out_3(out_13[7]));
  stone stone_33 (.whichone(C0), .choose(1'b1), .out_3(out_7[0]));
  stone stone_34 (.whichone(C1), .choose(1'b0), .out_3(out_7[1]));
  stone stone_35 (.whichone(C2), .choose(1'b0), .out_3(out_7[2]));
  stone stone_36 (.whichone(C3), .choose(1'b1), .out_3(out_7[3]));
  stone stone_37 (.whichone(C4), .choose(1'b0), .out_3(out_7[4]));
  stone stone_38 (.whichone(C5), .choose(1'b0), .out_3(out_7[5]));
  stone stone_39 (.whichone(C6), .choose(1'b0), .out_3(out_7[6]));
  stone stone_40 (.whichone(C7), .choose(1'b1), .out_3(out_7[7]));
  stone stone_41 (.whichone(D0), .choose(1'b1), .out_3(out_8[0]));
  stone stone_42 (.whichone(D1), .choose(1'b0), .out_3(out_8[1]));
  stone stone_43 (.whichone(D2), .choose(1'b0), .out_3(out_8[2]));
  stone stone_44 (.whichone(D3), .choose(1'b1), .out_3(out_8[3]));
  stone stone_45 (.whichone(D4), .choose(1'b0), .out_3(out_8[4]));
  stone stone_46 (.whichone(D5), .choose(1'b0), .out_3(out_8[5]));
  stone stone_47 (.whichone(D6), .choose(1'b0), .out_3(out_8[6]));
  stone stone_48 (.whichone(D7), .choose(1'b1), .out_3(out_8[7]));
  stone stone_49 (.whichone(E0), .choose(1'b1), .out_3(out_9[0]));
  stone stone_50 (.whichone(E1), .choose(1'b0), .out_3(out_9[1]));
  stone stone_51 (.whichone(E2), .choose(1'b0), .out_3(out_9[2]));
  stone stone_52 (.whichone(E3), .choose(1'b1), .out_3(out_9[3]));
  stone stone_53 (.whichone(E4), .choose(1'b0), .out_3(out_9[4]));
  stone stone_54 (.whichone(E5), .choose(1'b0), .out_3(out_9[5]));
  stone stone_55 (.whichone(E6), .choose(1'b0), .out_3(out_9[6]));
  stone stone_56 (.whichone(E7), .choose(1'b1), .out_3(out_9[7]));
  stone stone_57 (.whichone(F0), .choose(1'b1), .out_3(out_10[0]));
  stone stone_58 (.whichone(F1), .choose(1'b0), .out_3(out_10[1]));
  stone stone_59 (.whichone(F2), .choose(1'b0), .out_3(out_10[2]));
  stone stone_60 (.whichone(F3), .choose(1'b1), .out_3(out_10[3]));
  stone stone_61 (.whichone(F4), .choose(1'b0), .out_3(out_10[4]));
  stone stone_62 (.whichone(F5), .choose(1'b0), .out_3(out_10[5]));
  stone stone_63 (.whichone(F6), .choose(1'b0), .out_3(out_10[6]));
  stone stone_64 (.whichone(F7), .choose(1'b1), .out_3(out_10[7]));
endmodule

module U (
  input  S,
  input  T,
  input  CLK,
  input  R,
  output [7:0] A,
  output [7:0] out_6,
  output [7:0] out_7,
  output [7:0] out_8,
  output [7:0] out_9,
  output [7:0] out_10,
  output o,
  output [7:0] out_12,
  output [7:0] out_13
);

  wire A0, A1, A2, A3, A4, A5, A6, A7, B0, B1, B2, B3, B4, B5, B6, B7, C0, C1, C2, C3, C4, C5, C6, C7, D0,
       D1, D2, D3, D4, D5, D6, D7, E0, E1, E2, E3, E4, E5, E6, E7, F0, F1, F2, F3, F4, F5, F6, F7, G0, G1,
       G2, G3, G4, G5, G6, G7, H0, H1, H2, H3, H4, H5, H6, H7, t_ff_1_q;
  wire [7:0] bit_extender_1_out;

  T_Flip_Flop t_ff_1 (.T(T), .clk(CLK), .Q(t_ff_1_q), .Qn(o), .reset(R), .preset(S));
  assign bit_extender_1_out = {{7{t_ff_1_q}}, t_ff_1_q};  // Bit_Extender bit_extender_1
  assign {A7, A6, A5, A4, A3, A2, A1, A0} = {{7{bit_extender_1_out[0]}}, bit_extender_1_out[0]};  // Bit_Extender bit_extender_2
  assign {B7, B6, B5, B4, B3, B2, B1, B0} = {{7{bit_extender_1_out[1]}}, bit_extender_1_out[1]};  // Bit_Extender bit_extender_3
  assign {C7, C6, C5, C4, C3, C2, C1, C0} = {{7{bit_extender_1_out[2]}}, bit_extender_1_out[2]};  // Bit_Extender bit_extender_4
  assign {D7, D6, D5, D4, D3, D2, D1, D0} = {{7{bit_extender_1_out[3]}}, bit_extender_1_out[3]};  // Bit_Extender bit_extender_5
  assign {E7, E6, E5, E4, E3, E2, E1, E0} = {{7{bit_extender_1_out[4]}}, bit_extender_1_out[4]};  // Bit_Extender bit_extender_6
  assign {F7, F6, F5, F4, F3, F2, F1, F0} = {{7{bit_extender_1_out[5]}}, bit_extender_1_out[5]};  // Bit_Extender bit_extender_7
  assign {G7, G6, G5, G4, G3, G2, G1, G0} = {{7{bit_extender_1_out[6]}}, bit_extender_1_out[6]};  // Bit_Extender bit_extender_8
  assign {H7, H6, H5, H4, H3, H2, H1, H0} = {{7{bit_extender_1_out[7]}}, bit_extender_1_out[7]};  // Bit_Extender bit_extender_9
  stone stone_1 (.whichone(A0), .choose(1'b1), .out_3(A[0]));
  stone stone_2 (.whichone(A1), .choose(1'b1), .out_3(A[1]));
  stone stone_3 (.whichone(A2), .choose(1'b1), .out_3(A[2]));
  stone stone_4 (.whichone(A3), .choose(1'b1), .out_3(A[3]));
  stone stone_5 (.whichone(A4), .choose(1'b1), .out_3(A[4]));
  stone stone_6 (.whichone(A5), .choose(1'b1), .out_3(A[5]));
  stone stone_7 (.whichone(A6), .choose(1'b1), .out_3(A[6]));
  stone stone_8 (.whichone(A7), .choose(1'b1), .out_3(A[7]));
  stone stone_9 (.whichone(G0), .choose(1'b1), .out_3(out_12[0]));
  stone stone_10 (.whichone(G1), .choose(1'b0), .out_3(out_12[1]));
  stone stone_11 (.whichone(G2), .choose(1'b0), .out_3(out_12[2]));
  stone stone_12 (.whichone(G3), .choose(1'b0), .out_3(out_12[3]));
  stone stone_13 (.whichone(G4), .choose(1'b0), .out_3(out_12[4]));
  stone stone_14 (.whichone(G5), .choose(1'b0), .out_3(out_12[5]));
  stone stone_15 (.whichone(G6), .choose(1'b0), .out_3(out_12[6]));
  stone stone_16 (.whichone(G7), .choose(1'b0), .out_3(out_12[7]));
  stone stone_17 (.whichone(B0), .choose(1'b1), .out_3(out_6[0]));
  stone stone_18 (.whichone(B1), .choose(1'b0), .out_3(out_6[1]));
  stone stone_19 (.whichone(B2), .choose(1'b0), .out_3(out_6[2]));
  stone stone_20 (.whichone(B3), .choose(1'b0), .out_3(out_6[3]));
  stone stone_21 (.whichone(B4), .choose(1'b0), .out_3(out_6[4]));
  stone stone_22 (.whichone(B5), .choose(1'b0), .out_3(out_6[5]));
  stone stone_23 (.whichone(B6), .choose(1'b0), .out_3(out_6[6]));
  stone stone_24 (.whichone(B7), .choose(1'b0), .out_3(out_6[7]));
  stone stone_25 (.whichone(H0), .choose(1'b1), .out_3(out_13[0]));
  stone stone_26 (.whichone(H1), .choose(1'b1), .out_3(out_13[1]));
  stone stone_27 (.whichone(H2), .choose(1'b1), .out_3(out_13[2]));
  stone stone_28 (.whichone(H3), .choose(1'b1), .out_3(out_13[3]));
  stone stone_29 (.whichone(H4), .choose(1'b1), .out_3(out_13[4]));
  stone stone_30 (.whichone(H5), .choose(1'b1), .out_3(out_13[5]));
  stone stone_31 (.whichone(H6), .choose(1'b1), .out_3(out_13[6]));
  stone stone_32 (.whichone(H7), .choose(1'b1), .out_3(out_13[7]));
  stone stone_33 (.whichone(C0), .choose(1'b1), .out_3(out_7[0]));
  stone stone_34 (.whichone(C1), .choose(1'b0), .out_3(out_7[1]));
  stone stone_35 (.whichone(C2), .choose(1'b0), .out_3(out_7[2]));
  stone stone_36 (.whichone(C3), .choose(1'b0), .out_3(out_7[3]));
  stone stone_37 (.whichone(C4), .choose(1'b0), .out_3(out_7[4]));
  stone stone_38 (.whichone(C5), .choose(1'b0), .out_3(out_7[5]));
  stone stone_39 (.whichone(C6), .choose(1'b0), .out_3(out_7[6]));
  stone stone_40 (.whichone(C7), .choose(1'b0), .out_3(out_7[7]));
  stone stone_41 (.whichone(D0), .choose(1'b1), .out_3(out_8[0]));
  stone stone_42 (.whichone(D1), .choose(1'b0), .out_3(out_8[1]));
  stone stone_43 (.whichone(D2), .choose(1'b0), .out_3(out_8[2]));
  stone stone_44 (.whichone(D3), .choose(1'b0), .out_3(out_8[3]));
  stone stone_45 (.whichone(D4), .choose(1'b0), .out_3(out_8[4]));
  stone stone_46 (.whichone(D5), .choose(1'b0), .out_3(out_8[5]));
  stone stone_47 (.whichone(D6), .choose(1'b0), .out_3(out_8[6]));
  stone stone_48 (.whichone(D7), .choose(1'b0), .out_3(out_8[7]));
  stone stone_49 (.whichone(E0), .choose(1'b1), .out_3(out_9[0]));
  stone stone_50 (.whichone(E1), .choose(1'b0), .out_3(out_9[1]));
  stone stone_51 (.whichone(E2), .choose(1'b0), .out_3(out_9[2]));
  stone stone_52 (.whichone(E3), .choose(1'b0), .out_3(out_9[3]));
  stone stone_53 (.whichone(E4), .choose(1'b0), .out_3(out_9[4]));
  stone stone_54 (.whichone(E5), .choose(1'b0), .out_3(out_9[5]));
  stone stone_55 (.whichone(E6), .choose(1'b0), .out_3(out_9[6]));
  stone stone_56 (.whichone(E7), .choose(1'b0), .out_3(out_9[7]));
  stone stone_57 (.whichone(F0), .choose(1'b1), .out_3(out_10[0]));
  stone stone_58 (.whichone(F1), .choose(1'b0), .out_3(out_10[1]));
  stone stone_59 (.whichone(F2), .choose(1'b0), .out_3(out_10[2]));
  stone stone_60 (.whichone(F3), .choose(1'b0), .out_3(out_10[3]));
  stone stone_61 (.whichone(F4), .choose(1'b0), .out_3(out_10[4]));
  stone stone_62 (.whichone(F5), .choose(1'b0), .out_3(out_10[5]));
  stone stone_63 (.whichone(F6), .choose(1'b0), .out_3(out_10[6]));
  stone stone_64 (.whichone(F7), .choose(1'b0), .out_3(out_10[7]));
endmodule
